# Fritzing sketch arduino (saved by Fritzing 0.9.3b)

parts:
  Part2 = Arduino Uno (Rev3) - ICSP
  J1 = Basic Force Sensing Resistor (FSR) [package=THT]
  R1 = Resistor [tolerance=±5% resistance=120k package=THT]

nets:
  N1: Part2.A0, J1.pin_0, R1.Pin_1
  N2: Part2.5V, J1.pin_1
  N3: Part2.GND, R1.Pin_0
